# Fritzing sketch circuit diagram (saved by Fritzing 0.9.3b)

parts:
  U1 = RFID RC522 SIP - 8 pins [chip_label="RFID RC522" package="SIP (Single Inline) [THT]"]
  Part1 = Arduino Uno (Rev3) - ICSP
  Part2 = LCD1602-I2C
  VCC1 = Battery block 9V

nets:
  N1: U1.NSS, Part1.D10_PWM/SS
  N2: U1.SCK, Part1.D13/SCK
  N3: U1.MOSI, Part1.D11_PWM/MOSI
  N4: U1.MISO, Part1.D12/MISO
  GND: U1.GND, Part1.GND, Part2.GND, VCC1.-
  N5: U1.RST, Part1.D9_PWM
  VCC: U1.VCC, Part1.5V, Part2.VCC, VCC1.+
  N6: Part1.A4/SDA, Part2.SDA
  N7: Part1.A5/SCL, Part2.SCL

custom parts:
  RFID RC522 SIP - 8 pins: A SIP stand-in part for RFID RC522 . With 8 pins on a 300 mil single inline package (SIP) footprint.
  LCD1602-I2C: A standard character display, usually with 2x16 characters. Comes in many colors with LCM1602 IIC attached.
